# Fritzing sketch rez water level (saved by Fritzing 0.9.9b)
circuit board: 8.43508cm x 5.87609cm
breadboards: 1

parts:
  part = IC, DIP package, 6 pins [chip_label=HC12]
  ANT1 = Antenna
  R4 = Vertical Resistor [tolerance=±5% resistance=1M package=THT]
  R5 = Vertical Resistor [tolerance=±5% resistance=1M package=THT]
  R6 = Vertical Resistor [tolerance=±5% resistance=1M package=THT]
  part_2 = Arduino Nano (Rev3.0)

nets:
  N1: part.pin1, ANT1.antenna_lead
  N2: part.pin2, part_2.D0/RX
  N3: part.pin3, part_2.D1/TX
  N4: part.pin5, part_2.5V
  N5: part.pin6, part_2.GND
  N6: R4.Pin_0, part_2.D4
  N7: R4.Pin_1, part_2.D5
  N8: R5.Pin_0, part_2.D6
  N9: R5.Pin_1, part_2.D7
  N10: R6.Pin_0, part_2.D2
  N11: R6.Pin_1, part_2.D3

custom parts:
  Vertical Resistor: A generic resistor (0.25W)
